// Logisim project schiaccia_la_talpa.circ as structural Verilog: 8 circuits, main circuit Schiaccia la talpa
module Schiaccia_la_talpa (
  input  ON_OFF,
  input  _1,
  input  _2,
  input  _3,
  input  Ck,
  output T1,
  output T2,
  output T3,
  output Loss,
  output Win,
  output [3:0] Sx,
  output [3:0] Dx
);

  wire and_1_out, and_2_out, and_3_out, and_5_out, and_6_out, and_7_out, C, contatore_10_1_next,
       demultiplexer_1_out0, demultiplexer_1_out7, demultiplexer_1_out15, not_1_out, not_2_out, not_3_out,
       NT, or_1_out, or_2_out, or_3_out, or_4_out, S;
  wire [3:0] counter_1_q, random_1_out;

  Counter #(.width(4), .max('hf)) counter_1 (
    .count(not_1_out), .Q(counter_1_q), .clk(C), .clr(or_1_out));  // open: load, D, carry
  not not_1 (not_1_out, NT);
  Comparator #(.width(4)) comparator_1 (.a(4'b1000), .b(counter_1_q), .eq(Loss));  // open: gt, lt
  or or_1 (or_1_out, ~ON_OFF, S);  // OR_Gate
  and and_1 (and_1_out, _1, T1);
  and and_2 (and_2_out, _2, T2);
  and and_3 (and_3_out, _3, T3);
  ExactlyOne xor_1 (.out(S), .in1(and_1_out), .in2(and_2_out), .in3(and_3_out));
  and and_4 (C, Ck, ~Loss, ~Win, ON_OFF);  // AND_Gate
  Random #(.width(4)) random_1 (.clk(C), .out(random_1_out));  // open: next, clr
  Contatore_10 contatore_10_1 (.hit(S), .clock(C), .next(contatore_10_1_next), .bit_fino_a_9(Dx), .clear(not_3_out));
  Demultiplexer #(.select(4), .enable("false")) demultiplexer_1 (
    .out0(demultiplexer_1_out0), .out7(demultiplexer_1_out7), .out15(demultiplexer_1_out15), .in(1'b1),
    .sel(random_1_out));  // open: out1, out2, out3, out4, out5, out6, out8, out9, out10, out11, out12, out13, out14
  Contatore_10 contatore_10_2 (
    .hit(contatore_10_1_next), .clock(contatore_10_1_next), .bit_fino_a_9(Sx), .clear(not_2_out));  // open: next
  and and_5 (and_5_out, demultiplexer_1_out0, NT);
  and and_6 (and_6_out, demultiplexer_1_out7, NT);
  and and_7 (and_7_out, demultiplexer_1_out15, NT);
  and and_8 (NT, ~T1, ~T3, ~T2);  // AND_Gate
  D_Flip_Flop d_ff_1 (.clk(C), .D(and_5_out), .Q(T1), .en(or_2_out), .reset(Loss));  // open: Qn, preset
  or or_2 (or_2_out, and_5_out, S);
  D_Flip_Flop d_ff_2 (.clk(C), .D(and_6_out), .Q(T2), .en(or_3_out), .reset(Loss));  // open: Qn, preset
  or or_3 (or_3_out, and_6_out, S);
  or or_4 (or_4_out, and_7_out, S);
  D_Flip_Flop d_ff_3 (.clk(C), .D(and_7_out), .Q(T3), .en(or_4_out), .reset(Loss));  // open: Qn, preset
  not not_2 (not_2_out, ON_OFF);
  not not_3 (not_3_out, ON_OFF);
  Comparator #(.width(4)) comparator_2 (.a(Sx), .b(4'b0010), .eq(Win));  // open: gt, lt

  // Notes on the sheet:
  //   (A)
  //   (E)
  //   (F)
  //   (G)
  //   Ticks
  //   (B)
  //   (C)
  //   Se si spegne/riaccende si resetta
  //   Indica schiacciare la talpa quando è visibile
  //   Contatore 10
  //   Se si ha la score si resetta, invece se si perde si blocca il meccanismo di spawn
  //   (D)
  //   and con not talpa così ce ne può essere solo 1
  //   Se si vince si ferma lo spawn di talpe casuale in modo che non si possa più giocare
endmodule

module main (
  input  in_1,
  input  in_2
);

  wire _1, _2, _3, clock_1_out, clock_2_out, schiaccia_la_talpa_1_loss, schiaccia_la_talpa_1_win,
       \selettore_difficoltà_1_out , T1, T2, T3;
  wire [3:0] dx, sx;
  wire [6:0] w_l_display_1_out_3, w_l_display_1_out_4, w_l_display_1_out_5, w_l_display_1_out_6,
       w_l_display_1_out_7, w_l_display_1_out_8, w_l_display_1_out_9, w_l_display_1_out_10,
       w_l_display_1_out_11, w_l_display_1_out_12, w_l_display_1_out_13, w_l_display_1_out_14,
       w_l_display_1_out_15, w_l_display_1_out_16, w_l_display_1_out_17, w_l_display_1_out_18,
       w_l_display_1_out_19, w_l_display_1_out_20, w_l_display_1_out_21, w_l_display_1_out_22,
       w_l_display_1_out_23, w_l_display_1_out_24, w_l_display_1_out_25, w_l_display_1_out_26,
       w_l_display_1_out_27, w_l_display_1_out_28, w_l_display_1_out_29, w_l_display_1_out_30,
       w_l_display_1_out_31, w_l_display_1_out_32, w_l_display_1_out_33, w_l_display_1_out_34,
       w_l_display_1_out_35, w_l_display_1_out_36, w_l_display_1_out_37, w_l_display_1_out_38,
       w_l_display_1_out_39, w_l_display_1_out_40, w_l_display_1_out_41, w_l_display_1_out_42,
       w_l_display_1_out_43, w_l_display_1_out_44, w_l_display_1_out_45, w_l_display_1_out_46,
       w_l_display_1_out_47;
  wire [15:0] grafica_talpa_1_out_3, grafica_talpa_1_out_4, grafica_talpa_1_out_5, grafica_talpa_1_out_6,
       grafica_talpa_1_out_7, grafica_talpa_1_out_8, grafica_talpa_1_out_9, grafica_talpa_1_out_10,
       grafica_talpa_1_out_11, grafica_talpa_1_out_12, grafica_talpa_1_out_13, grafica_talpa_1_out_14,
       grafica_talpa_2_out_3, grafica_talpa_2_out_4, grafica_talpa_2_out_5, grafica_talpa_2_out_6,
       grafica_talpa_2_out_7, grafica_talpa_2_out_8, grafica_talpa_2_out_9, grafica_talpa_2_out_10,
       grafica_talpa_2_out_11, grafica_talpa_2_out_12, grafica_talpa_2_out_13, grafica_talpa_2_out_14,
       grafica_talpa_3_out_3, grafica_talpa_3_out_4, grafica_talpa_3_out_5, grafica_talpa_3_out_6,
       grafica_talpa_3_out_7, grafica_talpa_3_out_8, grafica_talpa_3_out_9, grafica_talpa_3_out_10,
       grafica_talpa_3_out_11, grafica_talpa_3_out_12, grafica_talpa_3_out_13, grafica_talpa_3_out_14;

  Clock #(.highDuration(5), .lowDuration(5)) clock_1 (.out(clock_1_out));
  Clock clock_2 (.out(clock_2_out));
  Hex_Digit_Display hex_digit_display_1 (.value(sx));  // open: dp
  \Selettore_difficoltà  \selettore_difficoltà_1  (
    .Clock1(clock_1_out), .sel1(in_2), .Clock2(clock_2_out), .out(\selettore_difficoltà_1_out ));
  Schiaccia_la_talpa schiaccia_la_talpa_1 (
    ._1(_1), ._2(_2), .T1(T1), .T2(T2), .T3(T3), ._3(_3), .Sx(sx), .Dx(dx),
    .Ck(\selettore_difficoltà_1_out ), .Win(schiaccia_la_talpa_1_win), .ON_OFF(in_1),
    .Loss(schiaccia_la_talpa_1_loss));
  Hex_Digit_Display hex_digit_display_2 (.value(dx));  // open: dp
  DotMatrix #(.matrixcols(12), .matrixrows(16)) dotmatrix_1 (
    .col0(grafica_talpa_1_out_3), .col1(grafica_talpa_1_out_4), .col2(grafica_talpa_1_out_5),
    .col3(grafica_talpa_1_out_6), .col4(grafica_talpa_1_out_7), .col5(grafica_talpa_1_out_8),
    .col6(grafica_talpa_1_out_9), .col7(grafica_talpa_1_out_10), .col8(grafica_talpa_1_out_11),
    .col9(grafica_talpa_1_out_12), .col10(grafica_talpa_1_out_13), .col11(grafica_talpa_1_out_14));
  Grafica_talpa grafica_talpa_1 (
    .hit(T1), .ON_OFF(in_1), .out_3(grafica_talpa_1_out_3), .out_4(grafica_talpa_1_out_4),
    .out_5(grafica_talpa_1_out_5), .out_6(grafica_talpa_1_out_6), .out_7(grafica_talpa_1_out_7),
    .out_8(grafica_talpa_1_out_8), .out_9(grafica_talpa_1_out_9), .out_10(grafica_talpa_1_out_10),
    .out_11(grafica_talpa_1_out_11), .out_12(grafica_talpa_1_out_12), .out_13(grafica_talpa_1_out_13),
    .out_14(grafica_talpa_1_out_14));
  DotMatrix #(.matrixcols(32)) dotmatrix_2 (
    .col0(w_l_display_1_out_3), .col1(w_l_display_1_out_4), .col2(w_l_display_1_out_5),
    .col3(w_l_display_1_out_6), .col4(w_l_display_1_out_7), .col5(w_l_display_1_out_8),
    .col6(w_l_display_1_out_9), .col7(w_l_display_1_out_10), .col8(w_l_display_1_out_11),
    .col9(w_l_display_1_out_12), .col10(w_l_display_1_out_13), .col11(w_l_display_1_out_14),
    .col12(w_l_display_1_out_15), .col13(w_l_display_1_out_16), .col14(w_l_display_1_out_17),
    .col15(w_l_display_1_out_18), .col16(w_l_display_1_out_19), .col17(w_l_display_1_out_20),
    .col18(w_l_display_1_out_21), .col19(w_l_display_1_out_22), .col20(w_l_display_1_out_23),
    .col21(w_l_display_1_out_24), .col22(w_l_display_1_out_25), .col23(w_l_display_1_out_26),
    .col24(w_l_display_1_out_27), .col25(w_l_display_1_out_28), .col26(w_l_display_1_out_29),
    .col27(w_l_display_1_out_30), .col28(w_l_display_1_out_31), .col29(w_l_display_1_out_32),
    .col30(w_l_display_1_out_33), .col31(w_l_display_1_out_34));
  W_L_Display w_l_display_1 (
    .win(schiaccia_la_talpa_1_win), .out_3(w_l_display_1_out_3), .out_4(w_l_display_1_out_4),
    .out_5(w_l_display_1_out_5), .out_6(w_l_display_1_out_6), .out_7(w_l_display_1_out_7),
    .out_8(w_l_display_1_out_8), .out_9(w_l_display_1_out_9), .out_10(w_l_display_1_out_10),
    .out_11(w_l_display_1_out_11), .out_12(w_l_display_1_out_12), .out_13(w_l_display_1_out_13),
    .out_14(w_l_display_1_out_14), .out_15(w_l_display_1_out_15), .out_16(w_l_display_1_out_16),
    .out_17(w_l_display_1_out_17), .out_18(w_l_display_1_out_18), .out_19(w_l_display_1_out_19),
    .out_20(w_l_display_1_out_20), .out_21(w_l_display_1_out_21), .out_22(w_l_display_1_out_22),
    .out_23(w_l_display_1_out_23), .out_24(w_l_display_1_out_24), .out_25(w_l_display_1_out_25),
    .out_26(w_l_display_1_out_26), .out_27(w_l_display_1_out_27), .out_28(w_l_display_1_out_28),
    .out_29(w_l_display_1_out_29), .out_30(w_l_display_1_out_30), .out_32(w_l_display_1_out_32),
    .out_33(w_l_display_1_out_33), .out_34(w_l_display_1_out_34), .out_35(w_l_display_1_out_35),
    .out_36(w_l_display_1_out_36), .out_37(w_l_display_1_out_37), .out_38(w_l_display_1_out_38),
    .out_39(w_l_display_1_out_39), .out_40(w_l_display_1_out_40), .out_41(w_l_display_1_out_41),
    .out_42(w_l_display_1_out_42), .out_43(w_l_display_1_out_43), .out_44(w_l_display_1_out_44),
    .out_46(w_l_display_1_out_46), .loss(schiaccia_la_talpa_1_loss), .out_31(w_l_display_1_out_31),
    .out_45(w_l_display_1_out_45), .out_47(w_l_display_1_out_47));
  DotMatrix #(.matrixcols(12), .matrixrows(16)) dotmatrix_3 (
    .col0(grafica_talpa_2_out_3), .col1(grafica_talpa_2_out_4), .col2(grafica_talpa_2_out_5),
    .col3(grafica_talpa_2_out_6), .col4(grafica_talpa_2_out_7), .col5(grafica_talpa_2_out_8),
    .col6(grafica_talpa_2_out_9), .col7(grafica_talpa_2_out_10), .col8(grafica_talpa_2_out_11),
    .col9(grafica_talpa_2_out_12), .col10(grafica_talpa_2_out_13), .col11(grafica_talpa_2_out_14));
  Grafica_talpa grafica_talpa_2 (
    .hit(T2), .ON_OFF(in_1), .out_3(grafica_talpa_2_out_3), .out_4(grafica_talpa_2_out_4),
    .out_5(grafica_talpa_2_out_5), .out_6(grafica_talpa_2_out_6), .out_7(grafica_talpa_2_out_7),
    .out_8(grafica_talpa_2_out_8), .out_9(grafica_talpa_2_out_9), .out_10(grafica_talpa_2_out_10),
    .out_11(grafica_talpa_2_out_11), .out_12(grafica_talpa_2_out_12), .out_13(grafica_talpa_2_out_13),
    .out_14(grafica_talpa_2_out_14));
  Button button_1 (.out(_1));
  Button button_2 (.out(_2));
  DotMatrix #(.matrixcols(12), .matrixrows(16)) dotmatrix_4 (
    .col0(grafica_talpa_3_out_3), .col1(grafica_talpa_3_out_4), .col2(grafica_talpa_3_out_5),
    .col3(grafica_talpa_3_out_6), .col4(grafica_talpa_3_out_7), .col5(grafica_talpa_3_out_8),
    .col6(grafica_talpa_3_out_9), .col7(grafica_talpa_3_out_10), .col8(grafica_talpa_3_out_11),
    .col9(grafica_talpa_3_out_12), .col10(grafica_talpa_3_out_13), .col11(grafica_talpa_3_out_14));
  Grafica_talpa grafica_talpa_3 (
    .hit(T3), .ON_OFF(in_1), .out_3(grafica_talpa_3_out_3), .out_4(grafica_talpa_3_out_4),
    .out_5(grafica_talpa_3_out_5), .out_6(grafica_talpa_3_out_6), .out_7(grafica_talpa_3_out_7),
    .out_8(grafica_talpa_3_out_8), .out_9(grafica_talpa_3_out_9), .out_10(grafica_talpa_3_out_10),
    .out_11(grafica_talpa_3_out_11), .out_12(grafica_talpa_3_out_12), .out_13(grafica_talpa_3_out_13),
    .out_14(grafica_talpa_3_out_14));
  Button button_3 (.out(_3));
  DotMatrix #(.matrixcols(13)) dotmatrix_5 (
    .col0(w_l_display_1_out_35), .col1(w_l_display_1_out_36), .col2(w_l_display_1_out_37),
    .col3(w_l_display_1_out_38), .col4(w_l_display_1_out_39), .col5(w_l_display_1_out_40),
    .col6(w_l_display_1_out_41), .col7(w_l_display_1_out_42), .col8(w_l_display_1_out_43),
    .col9(w_l_display_1_out_44), .col10(w_l_display_1_out_45), .col11(w_l_display_1_out_46),
    .col12(w_l_display_1_out_47));

  // Other names for the same wires on the sheet: ON_OFF = in_1

  // Notes on the sheet:
  //   Come giocare:
  //   1) selezionare livello difficoltà
  //   2) impostare a 1 ON/OFF
  //   3) premere il bottone corrispondente alla
  //   posizione nella quale compare la talpa
  //   4) impostare a 0 ON/OFF per spegnere
  //   Score
endmodule

module Grafica_talpa (
  input  hit,
  input  ON_OFF,
  output [15:0] out_3,
  output [15:0] out_4,
  output [15:0] out_5,
  output [15:0] out_6,
  output [15:0] out_7,
  output [15:0] out_8,
  output [15:0] out_9,
  output [15:0] out_10,
  output [15:0] out_11,
  output [15:0] out_12,
  output [15:0] out_13,
  output [15:0] out_14
);

  wire and_1_out;

  and and_1 (and_1_out, hit, ON_OFF);
  Multiplexer #(.width(16)) multiplexer_1 (
    .in0({16{1'b0}}), .in1({16{1'b0}}), .out(out_3), .sel(and_1_out));  // open: en
  Multiplexer #(.width(16)) multiplexer_2 (.in0({16{1'b0}}), .in1(16'h7ffe), .out(out_4), .sel(and_1_out));  // open: en
  Multiplexer #(.width(16)) multiplexer_3 (.in0({16{1'b0}}), .in1(16'h4002), .out(out_5), .sel(and_1_out));  // open: en
  Multiplexer #(.width(16)) multiplexer_4 (.in0({16{1'b0}}), .in1(16'h4002), .out(out_6), .sel(and_1_out));  // open: en
  Multiplexer #(.width(16)) multiplexer_5 (.in0({16{1'b0}}), .in1(16'h501a), .out(out_7), .sel(and_1_out));  // open: en
  Multiplexer #(.width(16)) multiplexer_6 (.in0({16{1'b0}}), .in1(16'h400a), .out(out_8), .sel(and_1_out));  // open: en
  Multiplexer #(.width(16)) multiplexer_7 (.in0({16{1'b0}}), .in1(16'h400a), .out(out_9), .sel(and_1_out));  // open: en
  Multiplexer #(.width(16)) multiplexer_8 (
    .in0({16{1'b0}}), .in1(16'h501a), .out(out_10), .sel(and_1_out));  // open: en
  Multiplexer #(.width(16)) multiplexer_9 (
    .in0({16{1'b0}}), .in1(16'h4002), .out(out_11), .sel(and_1_out));  // open: en
  Multiplexer #(.width(16)) multiplexer_10 (
    .in0({16{1'b0}}), .in1(16'h4002), .out(out_12), .sel(and_1_out));  // open: en
  Multiplexer #(.width(16)) multiplexer_11 (
    .in0({16{1'b0}}), .in1(16'h7ffe), .out(out_13), .sel(and_1_out));  // open: en
  Multiplexer #(.width(16)) multiplexer_12 (
    .in0({16{1'b0}}), .in1({16{1'b0}}), .out(out_14), .sel(and_1_out));  // open: en
endmodule

module Gestore_riporti (
  input  b3,
  input  b2,
  input  b1,
  input  b0,
  output next,
  output y3,
  output y2,
  output y1,
  output y0
);

  wire and_1_out, and_2_out, and_3_out, and_4_out, and_5_out, and_6_out, not_1_out, not_2_out;

  and and_1 (and_1_out, b3, b1);
  and and_2 (and_2_out, b3, b2);
  and and_3 (and_3_out, b3, not_1_out);
  not not_1 (not_1_out, b1);
  and and_4 (and_4_out, b3, b2);
  not not_2 (not_2_out, b3);
  and and_5 (and_5_out, not_2_out, b1);
  and and_6 (and_6_out, b3, b2);
  or or_1 (next, and_1_out, and_2_out);
  or or_2 (y3, and_3_out, and_4_out);
  or or_3 (y1, and_5_out, and_6_out);

  assign y0 = b0;
  assign y2 = b2;
endmodule

module Contatore_10 (
  input  hit,
  input  clear,
  input  clock,
  output next,
  output [3:0] bit_fino_a_9
);

  wire comparator_1_eq, or_1_out;
  wire [3:0] counter_1_q;

  Counter #(.width(4), .max('hf)) counter_1 (
    .count(hit), .Q(counter_1_q), .clk(clock), .clr(or_1_out));  // open: load, D, carry
  Gestore_riporti gestore_riporti_1 (
    .b3(counter_1_q[3]), .b2(counter_1_q[2]), .b1(counter_1_q[1]), .b0(counter_1_q[0]), .next(next),
    .y3(bit_fino_a_9[3]), .y2(bit_fino_a_9[2]), .y1(bit_fino_a_9[1]), .y0(bit_fino_a_9[0]));
  or or_1 (or_1_out, clear, comparator_1_eq);
  Comparator #(.width(4)) comparator_1 (.a(4'b1010), .b(counter_1_q), .eq(comparator_1_eq));  // open: gt, lt

  // Notes on the sheet:
  //   Gestore riporti
endmodule

module W_L_Display (
  input  win,
  input  loss,
  output [6:0] out_3,
  output [6:0] out_4,
  output [6:0] out_5,
  output [6:0] out_6,
  output [6:0] out_7,
  output [6:0] out_8,
  output [6:0] out_9,
  output [6:0] out_10,
  output [6:0] out_11,
  output [6:0] out_12,
  output [6:0] out_13,
  output [6:0] out_14,
  output [6:0] out_15,
  output [6:0] out_16,
  output [6:0] out_17,
  output [6:0] out_18,
  output [6:0] out_19,
  output [6:0] out_20,
  output [6:0] out_21,
  output [6:0] out_22,
  output [6:0] out_23,
  output [6:0] out_24,
  output [6:0] out_25,
  output [6:0] out_26,
  output [6:0] out_27,
  output [6:0] out_28,
  output [6:0] out_29,
  output [6:0] out_30,
  output [6:0] out_31,
  output [6:0] out_32,
  output [6:0] out_33,
  output [6:0] out_34,
  output [6:0] out_35,
  output [6:0] out_36,
  output [6:0] out_37,
  output [6:0] out_38,
  output [6:0] out_39,
  output [6:0] out_40,
  output [6:0] out_41,
  output [6:0] out_42,
  output [6:0] out_43,
  output [6:0] out_44,
  output [6:0] out_45,
  output [6:0] out_46,
  output [6:0] out_47
);

  wire [6:0] multiplexer_1_out, multiplexer_2_out, multiplexer_3_out, multiplexer_4_out, multiplexer_5_out,
       multiplexer_6_out, multiplexer_7_out, multiplexer_8_out, multiplexer_9_out, multiplexer_10_out,
       multiplexer_11_out, multiplexer_12_out, multiplexer_13_out, multiplexer_14_out, multiplexer_15_out,
       multiplexer_16_out, multiplexer_17_out, multiplexer_18_out, multiplexer_19_out, multiplexer_20_out,
       multiplexer_21_out, multiplexer_22_out, multiplexer_23_out, multiplexer_24_out, multiplexer_25_out,
       multiplexer_26_out, multiplexer_27_out, multiplexer_28_out, multiplexer_29_out, multiplexer_30_out,
       multiplexer_31_out, multiplexer_32_out, multiplexer_33_out, multiplexer_34_out, multiplexer_35_out,
       multiplexer_36_out, multiplexer_37_out, multiplexer_38_out, multiplexer_39_out, multiplexer_40_out,
       multiplexer_41_out, multiplexer_42_out, multiplexer_43_out, multiplexer_44_out, multiplexer_45_out,
       multiplexer_46_out, multiplexer_47_out, multiplexer_48_out, multiplexer_49_out, multiplexer_50_out,
       multiplexer_51_out, multiplexer_52_out, multiplexer_53_out, multiplexer_54_out, multiplexer_55_out,
       multiplexer_56_out, multiplexer_57_out, multiplexer_58_out, multiplexer_59_out, multiplexer_60_out,
       multiplexer_61_out, multiplexer_62_out, multiplexer_63_out, multiplexer_64_out, multiplexer_65_out,
       multiplexer_66_out, multiplexer_67_out, multiplexer_68_out, multiplexer_69_out, multiplexer_70_out,
       multiplexer_71_out, multiplexer_72_out, multiplexer_73_out, multiplexer_74_out, multiplexer_75_out,
       multiplexer_76_out, multiplexer_77_out, multiplexer_78_out, multiplexer_79_out, multiplexer_80_out,
       multiplexer_81_out, multiplexer_82_out, multiplexer_83_out, multiplexer_84_out, multiplexer_85_out,
       multiplexer_86_out, multiplexer_87_out, multiplexer_88_out, multiplexer_89_out, multiplexer_90_out;

  Multiplexer #(.width(7)) multiplexer_1 (
    .in0({7{1'b0}}), .in1({7{1'b1}}), .out(multiplexer_1_out), .sel(win));  // open: en
  Multiplexer #(.width(7)) multiplexer_2 (
    .in0({7{1'b0}}), .in1({7{1'b1}}), .out(multiplexer_2_out), .sel(loss));  // open: en
  assign out_3 = multiplexer_1_out | multiplexer_2_out;  // OR_Gate or_1, 7 bits wide
  assign out_4 = multiplexer_3_out | multiplexer_4_out;  // OR_Gate or_2, 7 bits wide
  Multiplexer #(.width(7)) multiplexer_3 (
    .in0({7{1'b0}}), .in1(7'b0001000), .out(multiplexer_3_out), .sel(win));  // open: en
  Multiplexer #(.width(7)) multiplexer_4 (
    .in0({7{1'b0}}), .in1(7'b0001000), .out(multiplexer_4_out), .sel(loss));  // open: en
  Multiplexer #(.width(7)) multiplexer_5 (
    .in0({7{1'b0}}), .in1(7'b0001000), .out(multiplexer_5_out), .sel(loss));  // open: en
  assign out_5 = multiplexer_6_out | multiplexer_5_out;  // OR_Gate or_3, 7 bits wide
  Multiplexer #(.width(7)) multiplexer_6 (
    .in0({7{1'b0}}), .in1(7'b0001000), .out(multiplexer_6_out), .sel(win));  // open: en
  Multiplexer #(.width(7)) multiplexer_7 (
    .in0({7{1'b0}}), .in1({7{1'b1}}), .out(multiplexer_7_out), .sel(loss));  // open: en
  assign out_6 = multiplexer_8_out | multiplexer_7_out;  // OR_Gate or_4, 7 bits wide
  Multiplexer #(.width(7)) multiplexer_8 (
    .in0({7{1'b0}}), .in1({7{1'b1}}), .out(multiplexer_8_out), .sel(win));  // open: en
  Multiplexer #(.width(7)) multiplexer_9 (
    .in0({7{1'b0}}), .in1({7{1'b0}}), .out(multiplexer_9_out), .sel(win));  // open: en
  Multiplexer #(.width(7)) multiplexer_10 (
    .in0({7{1'b0}}), .in1({7{1'b0}}), .out(multiplexer_10_out), .sel(loss));  // open: en
  Multiplexer #(.width(7)) multiplexer_11 (
    .in0({7{1'b0}}), .in1(7'b0000011), .out(multiplexer_11_out), .sel(loss));  // open: en
  assign out_7 = multiplexer_9_out | multiplexer_10_out;  // OR_Gate or_5, 7 bits wide
  Multiplexer #(.width(7)) multiplexer_12 (
    .in0({7{1'b0}}), .in1(7'b0000011), .out(multiplexer_12_out), .sel(win));  // open: en
  Multiplexer #(.width(7)) multiplexer_13 (
    .in0({7{1'b0}}), .in1(7'b0001100), .out(multiplexer_13_out), .sel(win));  // open: en
  Multiplexer #(.width(7)) multiplexer_14 (
    .in0({7{1'b0}}), .in1(7'b0001100), .out(multiplexer_14_out), .sel(loss));  // open: en
  assign out_8 = multiplexer_12_out | multiplexer_11_out;  // OR_Gate or_6, 7 bits wide
  Multiplexer #(.width(7)) multiplexer_15 (
    .in0({7{1'b0}}), .in1(7'b0111000), .out(multiplexer_15_out), .sel(win));  // open: en
  Multiplexer #(.width(7)) multiplexer_16 (
    .in0({7{1'b0}}), .in1(7'b0111000), .out(multiplexer_16_out), .sel(loss));  // open: en
  Multiplexer #(.width(7)) multiplexer_17 (
    .in0({7{1'b0}}), .in1(7'b1001000), .out(multiplexer_17_out), .sel(loss));  // open: en
  assign out_9 = multiplexer_13_out | multiplexer_14_out;  // OR_Gate or_7, 7 bits wide
  Multiplexer #(.width(7)) multiplexer_18 (
    .in0({7{1'b0}}), .in1(7'b1001000), .out(multiplexer_18_out), .sel(win));  // open: en
  Multiplexer #(.width(7)) multiplexer_19 (
    .in0({7{1'b0}}), .in1(7'b1001000), .out(multiplexer_19_out), .sel(win));  // open: en
  Multiplexer #(.width(7)) multiplexer_20 (
    .in0({7{1'b0}}), .in1(7'b1001000), .out(multiplexer_20_out), .sel(loss));  // open: en
  assign out_10 = multiplexer_15_out | multiplexer_16_out;  // OR_Gate or_8, 7 bits wide
  assign out_11 = multiplexer_18_out | multiplexer_17_out;  // OR_Gate or_9, 7 bits wide
  Multiplexer #(.width(7)) multiplexer_21 (
    .in0({7{1'b0}}), .in1(7'b0111000), .out(multiplexer_21_out), .sel(win));  // open: en
  Multiplexer #(.width(7)) multiplexer_22 (
    .in0({7{1'b0}}), .in1(7'b0111000), .out(multiplexer_22_out), .sel(loss));  // open: en
  Multiplexer #(.width(7)) multiplexer_23 (
    .in0({7{1'b0}}), .in1(7'b0001100), .out(multiplexer_23_out), .sel(loss));  // open: en
  assign out_12 = multiplexer_19_out | multiplexer_20_out;  // OR_Gate or_10, 7 bits wide
  Multiplexer #(.width(7)) multiplexer_24 (
    .in0({7{1'b0}}), .in1(7'b0001100), .out(multiplexer_24_out), .sel(win));  // open: en
  Multiplexer #(.width(7)) multiplexer_25 (
    .in0({7{1'b0}}), .in1(7'b0000011), .out(multiplexer_25_out), .sel(loss));  // open: en
  assign out_13 = multiplexer_21_out | multiplexer_22_out;  // OR_Gate or_11, 7 bits wide
  Multiplexer #(.width(7)) multiplexer_26 (
    .in0({7{1'b0}}), .in1(7'b0000011), .out(multiplexer_26_out), .sel(win));  // open: en
  Multiplexer #(.width(7)) multiplexer_27 (
    .in0({7{1'b0}}), .in1({7{1'b0}}), .out(multiplexer_27_out), .sel(loss));  // open: en
  assign out_14 = multiplexer_24_out | multiplexer_23_out;  // OR_Gate or_12, 7 bits wide
  Multiplexer #(.width(7)) multiplexer_28 (
    .in0({7{1'b0}}), .in1({7{1'b0}}), .out(multiplexer_28_out), .sel(win));  // open: en
  Multiplexer #(.width(7)) multiplexer_29 (
    .in0({7{1'b0}}), .in1({7{1'b1}}), .out(multiplexer_29_out), .sel(win));  // open: en
  Multiplexer #(.width(7)) multiplexer_30 (
    .in0({7{1'b0}}), .in1({7{1'b1}}), .out(multiplexer_30_out), .sel(loss));  // open: en
  assign out_15 = multiplexer_26_out | multiplexer_25_out;  // OR_Gate or_13, 7 bits wide
  Multiplexer #(.width(7)) multiplexer_31 (
    .in0({7{1'b0}}), .in1({7{1'b0}}), .out(multiplexer_31_out), .sel(win));  // open: en
  Multiplexer #(.width(7)) multiplexer_32 (
    .in0({7{1'b0}}), .in1({7{1'b0}}), .out(multiplexer_32_out), .sel(loss));  // open: en
  assign out_16 = multiplexer_28_out | multiplexer_27_out;  // OR_Gate or_14, 7 bits wide
  Multiplexer #(.width(7)) multiplexer_33 (
    .in0({7{1'b0}}), .in1(7'b1100000), .out(multiplexer_33_out), .sel(win));  // open: en
  Multiplexer #(.width(7)) multiplexer_34 (
    .in0({7{1'b0}}), .in1({7{1'b1}}), .out(multiplexer_34_out), .sel(loss));  // open: en
  Multiplexer #(.width(7)) multiplexer_35 (
    .in0({7{1'b0}}), .in1(7'b1000100), .out(multiplexer_35_out), .sel(loss));  // open: en
  assign out_17 = multiplexer_29_out | multiplexer_30_out;  // OR_Gate or_15, 7 bits wide
  Multiplexer #(.width(7)) multiplexer_36 (
    .in0({7{1'b0}}), .in1(7'b0011000), .out(multiplexer_36_out), .sel(win));  // open: en
  Multiplexer #(.width(7)) multiplexer_37 (
    .in0({7{1'b0}}), .in1(7'b0101000), .out(multiplexer_37_out), .sel(loss));  // open: en
  assign out_19 = multiplexer_33_out | multiplexer_34_out;  // OR_Gate or_16, 7 bits wide
  assign out_18 = multiplexer_31_out | multiplexer_32_out;  // OR_Gate or_17, 7 bits wide
  Multiplexer #(.width(7)) multiplexer_38 (
    .in0({7{1'b0}}), .in1(7'b0010000), .out(multiplexer_38_out), .sel(loss));  // open: en
  assign out_20 = multiplexer_36_out | multiplexer_35_out;  // OR_Gate or_18, 7 bits wide
  Multiplexer #(.width(7)) multiplexer_39 (
    .in0({7{1'b0}}), .in1(7'b0000110), .out(multiplexer_39_out), .sel(win));  // open: en
  Multiplexer #(.width(7)) multiplexer_40 (
    .in0({7{1'b0}}), .in1(7'b0000001), .out(multiplexer_40_out), .sel(win));  // open: en
  Multiplexer #(.width(7)) multiplexer_41 (
    .in0({7{1'b0}}), .in1(7'b0000110), .out(multiplexer_41_out), .sel(win));  // open: en
  Multiplexer #(.width(7)) multiplexer_42 (
    .in0({7{1'b0}}), .in1({7{1'b0}}), .out(multiplexer_42_out), .sel(loss));  // open: en
  Multiplexer #(.width(7)) multiplexer_43 (
    .in0({7{1'b0}}), .in1({7{1'b1}}), .out(multiplexer_43_out), .sel(loss));  // open: en
  assign out_21 = multiplexer_39_out | multiplexer_37_out;  // OR_Gate or_19, 7 bits wide
  Multiplexer #(.width(7)) multiplexer_44 (
    .in0({7{1'b0}}), .in1(7'b0011000), .out(multiplexer_44_out), .sel(win));  // open: en
  Multiplexer #(.width(7)) multiplexer_45 (
    .in0({7{1'b0}}), .in1(7'b1001001), .out(multiplexer_45_out), .sel(loss));  // open: en
  assign out_22 = multiplexer_40_out | multiplexer_38_out;  // OR_Gate or_20, 7 bits wide
  Multiplexer #(.width(7)) multiplexer_46 (
    .in0({7{1'b0}}), .in1(7'b1100000), .out(multiplexer_46_out), .sel(win));  // open: en
  Multiplexer #(.width(7)) multiplexer_47 (
    .in0({7{1'b0}}), .in1(7'b1001001), .out(multiplexer_47_out), .sel(loss));  // open: en
  assign out_23 = multiplexer_41_out | multiplexer_42_out;  // OR_Gate or_21, 7 bits wide
  Multiplexer #(.width(7)) multiplexer_48 (
    .in0({7{1'b0}}), .in1({7{1'b0}}), .out(multiplexer_48_out), .sel(win));  // open: en
  Multiplexer #(.width(7)) multiplexer_49 (
    .in0({7{1'b0}}), .in1(7'b1000001), .out(multiplexer_49_out), .sel(loss));  // open: en
  assign out_24 = multiplexer_44_out | multiplexer_43_out;  // OR_Gate or_22, 7 bits wide
  Multiplexer #(.width(7)) multiplexer_50 (
    .in0({7{1'b0}}), .in1({7{1'b1}}), .out(multiplexer_50_out), .sel(win));  // open: en
  assign out_25 = multiplexer_46_out | multiplexer_45_out;  // OR_Gate or_23, 7 bits wide
  Multiplexer #(.width(7)) multiplexer_51 (
    .in0({7{1'b0}}), .in1({7{1'b0}}), .out(multiplexer_51_out), .sel(win));  // open: en
  Multiplexer #(.width(7)) multiplexer_52 (
    .in0({7{1'b0}}), .in1({7{1'b0}}), .out(multiplexer_52_out), .sel(loss));  // open: en
  Multiplexer #(.width(7)) multiplexer_53 (
    .in0({7{1'b0}}), .in1({7{1'b1}}), .out(multiplexer_53_out), .sel(loss));  // open: en
  assign out_27 = multiplexer_50_out | multiplexer_49_out;  // OR_Gate or_24, 7 bits wide
  assign out_26 = multiplexer_48_out | multiplexer_47_out;  // OR_Gate or_25, 7 bits wide
  Multiplexer #(.width(7)) multiplexer_54 (
    .in0({7{1'b0}}), .in1({7{1'b1}}), .out(multiplexer_54_out), .sel(win));  // open: en
  Multiplexer #(.width(7)) multiplexer_55 (
    .in0({7{1'b0}}), .in1(7'b1000100), .out(multiplexer_55_out), .sel(loss));  // open: en
  assign out_28 = multiplexer_51_out | multiplexer_52_out;  // OR_Gate or_26, 7 bits wide
  Multiplexer #(.width(7)) multiplexer_56 (
    .in0({7{1'b0}}), .in1(7'b1000000), .out(multiplexer_56_out), .sel(win));  // open: en
  assign out_29 = multiplexer_54_out | multiplexer_53_out;  // OR_Gate or_27, 7 bits wide
  Multiplexer #(.width(7)) multiplexer_57 (
    .in0({7{1'b0}}), .in1(7'b0110000), .out(multiplexer_57_out), .sel(win));  // open: en
  Multiplexer #(.width(7)) multiplexer_58 (
    .in0({7{1'b0}}), .in1(7'b0101010), .out(multiplexer_58_out), .sel(loss));  // open: en
  assign out_30 = multiplexer_56_out | multiplexer_55_out;  // OR_Gate or_28, 7 bits wide
  Multiplexer #(.width(7)) multiplexer_59 (
    .in0({7{1'b0}}), .in1(7'b0001100), .out(multiplexer_59_out), .sel(win));  // open: en
  Multiplexer #(.width(7)) multiplexer_60 (
    .in0({7{1'b0}}), .in1(7'b0010001), .out(multiplexer_60_out), .sel(loss));  // open: en
  assign out_31 = multiplexer_57_out | multiplexer_58_out;  // OR_Gate or_29, 7 bits wide
  Multiplexer #(.width(7)) multiplexer_61 (
    .in0({7{1'b0}}), .in1(7'b0000011), .out(multiplexer_61_out), .sel(win));  // open: en
  Multiplexer #(.width(7)) multiplexer_62 (
    .in0({7{1'b0}}), .in1({7{1'b0}}), .out(multiplexer_62_out), .sel(loss));  // open: en
  Multiplexer #(.width(7)) multiplexer_63 (
    .in0({7{1'b0}}), .in1(7'b0110001), .out(multiplexer_63_out), .sel(loss));  // open: en
  assign out_32 = multiplexer_59_out | multiplexer_60_out;  // OR_Gate or_30, 7 bits wide
  Multiplexer #(.width(7)) multiplexer_64 (
    .in0({7{1'b0}}), .in1({7{1'b1}}), .out(multiplexer_64_out), .sel(win));  // open: en
  Multiplexer #(.width(7)) multiplexer_65 (
    .in0({7{1'b0}}), .in1(7'b1001001), .out(multiplexer_65_out), .sel(loss));  // open: en
  assign out_33 = multiplexer_61_out | multiplexer_62_out;  // OR_Gate or_31, 7 bits wide
  Multiplexer #(.width(7)) multiplexer_66 (
    .in0({7{1'b0}}), .in1({7{1'b0}}), .out(multiplexer_66_out), .sel(win));  // open: en
  Multiplexer #(.width(7)) multiplexer_67 (
    .in0({7{1'b0}}), .in1(7'b1001001), .out(multiplexer_67_out), .sel(loss));  // open: en
  assign out_34 = multiplexer_64_out | multiplexer_63_out;  // OR_Gate or_32, 7 bits wide
  assign out_35 = multiplexer_66_out | multiplexer_65_out;  // OR_Gate or_33, 7 bits wide
  Multiplexer #(.width(7)) multiplexer_68 (
    .in0({7{1'b0}}), .in1(7'b1000000), .out(multiplexer_68_out), .sel(win));  // open: en
  Multiplexer #(.width(7)) multiplexer_69 (
    .in0({7{1'b0}}), .in1(7'b1000110), .out(multiplexer_69_out), .sel(loss));  // open: en
  assign out_36 = multiplexer_68_out | multiplexer_67_out;  // OR_Gate or_34, 7 bits wide
  Multiplexer #(.width(7)) multiplexer_70 (
    .in0({7{1'b0}}), .in1(7'b1000000), .out(multiplexer_70_out), .sel(win));  // open: en
  Multiplexer #(.width(7)) multiplexer_71 (
    .in0({7{1'b0}}), .in1({7{1'b0}}), .out(multiplexer_71_out), .sel(loss));  // open: en
  assign out_37 = multiplexer_70_out | multiplexer_69_out;  // OR_Gate or_35, 7 bits wide
  Multiplexer #(.width(7)) multiplexer_72 (
    .in0({7{1'b0}}), .in1({7{1'b1}}), .out(multiplexer_72_out), .sel(win));  // open: en
  Multiplexer #(.width(7)) multiplexer_73 (
    .in0({7{1'b0}}), .in1(7'b0011100), .out(multiplexer_73_out), .sel(loss));  // open: en
  assign out_38 = multiplexer_72_out | multiplexer_71_out;  // OR_Gate or_36, 7 bits wide
  Multiplexer #(.width(7)) multiplexer_74 (
    .in0({7{1'b0}}), .in1(7'b1000000), .out(multiplexer_74_out), .sel(win));  // open: en
  Multiplexer #(.width(7)) multiplexer_75 (
    .in0({7{1'b0}}), .in1(7'b0100010), .out(multiplexer_75_out), .sel(loss));  // open: en
  assign out_39 = multiplexer_74_out | multiplexer_73_out;  // OR_Gate or_37, 7 bits wide
  Multiplexer #(.width(7)) multiplexer_76 (
    .in0({7{1'b0}}), .in1(7'b1000000), .out(multiplexer_76_out), .sel(win));  // open: en
  Multiplexer #(.width(7)) multiplexer_77 (
    .in0({7{1'b0}}), .in1({7{1'b0}}), .out(multiplexer_77_out), .sel(win));  // open: en
  Multiplexer #(.width(7)) multiplexer_78 (
    .in0({7{1'b0}}), .in1(7'b1000001), .out(multiplexer_78_out), .sel(loss));  // open: en
  Multiplexer #(.width(7)) multiplexer_79 (
    .in0({7{1'b0}}), .in1(7'b1000001), .out(multiplexer_79_out), .sel(loss));  // open: en
  assign out_40 = multiplexer_76_out | multiplexer_75_out;  // OR_Gate or_38, 7 bits wide
  Multiplexer #(.width(7)) multiplexer_80 (
    .in0({7{1'b0}}), .in1(7'b0011100), .out(multiplexer_80_out), .sel(win));  // open: en
  Multiplexer #(.width(7)) multiplexer_81 (
    .in0({7{1'b0}}), .in1(7'b0100010), .out(multiplexer_81_out), .sel(loss));  // open: en
  assign out_41 = multiplexer_77_out | multiplexer_78_out;  // OR_Gate or_39, 7 bits wide
  Multiplexer #(.width(7)) multiplexer_82 (
    .in0({7{1'b0}}), .in1(7'b0100010), .out(multiplexer_82_out), .sel(win));  // open: en
  Multiplexer #(.width(7)) multiplexer_83 (
    .in0({7{1'b0}}), .in1(7'b0011100), .out(multiplexer_83_out), .sel(loss));  // open: en
  Multiplexer #(.width(7)) multiplexer_84 (
    .in0({7{1'b0}}), .in1({7{1'b0}}), .out(multiplexer_84_out), .sel(loss));  // open: en
  assign out_42 = multiplexer_80_out | multiplexer_79_out;  // OR_Gate or_40, 7 bits wide
  assign out_43 = multiplexer_82_out | multiplexer_81_out;  // OR_Gate or_41, 7 bits wide
  Multiplexer #(.width(7)) multiplexer_85 (
    .in0({7{1'b0}}), .in1(7'b1000001), .out(multiplexer_85_out), .sel(win));  // open: en
  Multiplexer #(.width(7)) multiplexer_86 (
    .in0({7{1'b0}}), .in1(7'b1000001), .out(multiplexer_86_out), .sel(win));  // open: en
  assign out_44 = multiplexer_85_out | multiplexer_83_out;  // OR_Gate or_42, 7 bits wide
  Multiplexer #(.width(7)) multiplexer_87 (
    .in0({7{1'b0}}), .in1(7'b0100010), .out(multiplexer_87_out), .sel(win));  // open: en
  Multiplexer #(.width(7)) multiplexer_88 (
    .in0({7{1'b0}}), .in1({7{1'b0}}), .out(multiplexer_88_out), .sel(loss));  // open: en
  assign out_45 = multiplexer_86_out | multiplexer_84_out;  // OR_Gate or_43, 7 bits wide
  Multiplexer #(.width(7)) multiplexer_89 (
    .in0({7{1'b0}}), .in1({7{1'b0}}), .out(multiplexer_89_out), .sel(loss));  // open: en
  assign out_46 = multiplexer_87_out | multiplexer_88_out;  // OR_Gate or_44, 7 bits wide
  Multiplexer #(.width(7)) multiplexer_90 (
    .in0({7{1'b0}}), .in1(7'b0011100), .out(multiplexer_90_out), .sel(win));  // open: en
  assign out_47 = multiplexer_90_out | multiplexer_89_out;  // OR_Gate or_45, 7 bits wide

  // Other names for the same wires on the sheet: _30 = win

  // Notes on the sheet:
  //   fefeefefefef
endmodule

module \Selettore_difficoltà  (
  input  Clock1,
  input  sel1,
  input  Clock2,
  output out
);

  wire and_1_out, and_2_out, not_1_out;

  not not_1 (not_1_out, sel1);
  and and_1 (and_1_out, Clock1, not_1_out);
  and and_2 (and_2_out, sel1, Clock2);
  or or_1 (out, and_1_out, and_2_out);
endmodule

module \new  (
  output [6:0] out_1
);

  DotMatrix dotmatrix_1 (.col0(7'b1111100), .col1(7'b0000011), .col2(7'b0001100), .col3(7'b0000011), .col4(7'b1111100));
  DotMatrix dotmatrix_2 (.col0({7{1'b1}}), .col1(7'b0000001), .col2(7'b0000001), .col3(7'b0000001), .col4(7'b0000001));
  DotMatrix dotmatrix_3 (.col0(7'b0011100), .col1(7'b0100010), .col2(7'b1000001), .col3(7'b0100010), .col4(7'b0011100));
endmodule
